# Fritzing sketch schematic (saved by Fritzing 1.0.6)
breadboards: 1

parts:
  Part1 = Adafruit Flora [part_number="Adafruit #659"]
  Part2 = Flora LSM303 Compass+Accel
  Raspberry_Pi1 = Raspberry Pi 2
  Part3 = Logic Level Converter

nets:
  +3V3: Part1.+3V3, Part2.3.3V, Part3.LV
  GND: Part1.GND, Part2.GND, Raspberry_Pi1.GND, Part3.GND
  N1: Part1.MISO, Part3.RX2_LV
  N2: Part1.SCK, Part3.RX_LV
  N3: Part1.MOSI, Part3.TX_LV
  N4: Part1.IO2/SDA, Part2.SCL
  N5: Part1.IO3/SCL, Part2.SDA
  N6: Raspberry_Pi1.GPIO10, Part3.TX_HV
  N7: Raspberry_Pi1.GPIO9, Part3.RX2_HV
  N8: Raspberry_Pi1.GPIO11, Part3.RX_HV
  N9: Raspberry_Pi1.5V, Part3.HV

notes:
  Guitar strings should be connected to breadboard columns 1-6, frets to columns 7-10.
  The frets should connect to pins 32, 36, 33 and 31 on the RPi. The strings should connect to pins 11, 13, 15, 12, 16 and 18.

custom parts:
  Adafruit Flora: FLORA is Adafruit's fully-featured wearable electronics platform. It's a round, sewable, Arduino-compatible microcontroller designed to empower amazing wearables projects. The FLORA is small (1.75" diameter, weighing 4.4 grams). The FLORA has built-in USB support. Built in USB means you plug it in to program it, it just shows up - all you need is a Micro-B USB cable, no additional purchases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
  Flora LSM303 Compass+Accel: Add motion and direction sensing to your wearable FLORA project with this high precision 3-axis Accelerometer+Compass sensor. Inside are two sensors, one is a classic 3-axis accelerometer, which can tell you which direction is down towards the Earth (by measuring gravity) or how fast the board is accelerating in 3D space. The other is a magnetometer that can sense where the strongest magnetic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
